# Fritzing sketch Set_TWP_By_Nano_M3_CB(18x24)-PCB(46x64) (saved by Fritzing 0.9.10b)
circuit board: 4.6cm x 6.4cm
perfboards: 1

parts:
  NanoV3_0 = Arduino Nano (Rev3.0)
  V1 = AMS1777 3.3V regulator module [part_number=3.3V稳压模块 package=module]
  Squix1 = OLED 0.91" 128x32 I2C SSD1306 (GND/VCC)
  uSD_holder1 = KCL microSD shield
  S1 = Pushbutton [part_number=检查TWP package="[THT]"]
  S2 = Pushbutton [part_number=启用TWP package="[THT]"]
  S3 = Pushbutton [part_number=取消TWP package="[THT]"]

nets:
  GND: NanoV3_0.GND, V1.GND-_(input), V1.GND-_(output), Squix1.GND, uSD_holder1.GND, S1.Pin_1, S1.Pin_2, S2.Pin_1, S2.Pin_2, S3.Pin_1, S3.Pin_2
  N1: NanoV3_0.D2, S1.Pin_3, S1.Pin_4
  N2: NanoV3_0.D3, S2.Pin_3, S2.Pin_4
  N3: NanoV3_0.D4, S3.Pin_3, S3.Pin_4
  N4: NanoV3_0.D10, uSD_holder1.CS
  N5: NanoV3_0.D11/MOSI, uSD_holder1.MOSI
  N6: NanoV3_0.D12/MISO, uSD_holder1.MISO
  5V: NanoV3_0.5V, V1.VIN+, Squix1.VCC
  N7: NanoV3_0.A5, Squix1.SCL
  N8: NanoV3_0.A4, Squix1.SCA
  N9: NanoV3_0.D13/SCK, uSD_holder1.CLK
  N10: V1.VOUT+, uSD_holder1.3V3

custom parts:
  OLED 0.91" 128x32 I2C SSD1306 (GND/VCC): OLED 0.91" 128x32 I2C SSD1306 Pinout: GND/VCC/SCL/SDA
  KCL microSD shield: KCL microSD shield Fritzing part for the commonly available mass-produced microSD card shields. MicroSD cards are inserted on the underside of the device with the connectors facing up. Creative Common Attribution 4.0 International (CC-BY 4.0) license. Any use of this part requires attribution of Dr Kristofer Chan, Department of Geography, King's College London. Contact kristofer.chan [at]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
